// Logisim project ProiectVLSI - Modif.circ as structural Verilog: 14 circuits, main circuit main
module main (
  input  in_1
);

  wire A, alu_1_cout, B, C, clc, CLK, count, flags, IN, IR, keyboard_1_avail, ld, ldcount, mar, not_1_out,
       not_2_out, or_1_out, OUT, str, x;
  wire [2:0] bus, counter_1_q, OPC;
  wire [3:0] IR_q_2;
  wire [6:0] keyboard_1_data;
  wire [7:0] DATA_IN, IN_q, OUT_A, OUT_ALU, OUT_B, OUT_C, OUT_MAR, OUT_q, PC_q, ram_1_data, subtractor_1_out;
  wire [7:4] IR_q;
  wire [7:7] or_2_out;

  Keyboard #(.buflen(8)) keyboard_1 (.clk(CLK), .re(IN), .clr(in_1), .avail(keyboard_1_avail), .data(keyboard_1_data));
  Clock clock_1 (.out(CLK));
  not not_1 (not_1_out, CLK);
  Counter #(.width(3), .max('h7)) counter_1 (
    .count(1'b1), .Q(counter_1_q), .clk(not_1_out), .clr(or_1_out));  // open: load, D, carry
  or or_1 (or_1_out, in_1, clc);
  not not_2 (not_2_out, keyboard_1_avail);
  or or_2 (or_2_out[7], not_2_out, alu_1_cout);
  Subtractor subtractor_1 (.a({1'b0, keyboard_1_data}), .b(8'h30), .out(subtractor_1_out));  // open: bin, bout
  ALU alu_1 (.a(OUT_A), .b(OUT_B), .Cin(OPC[0]), .out(OUT_ALU), .Cout(alu_1_cout));
  Register u_MAR (.D(DATA_IN), .en(mar), .Q(OUT_MAR), .clk(CLK), .clr(in_1));
  Counter PC (.load(ldcount), .D(DATA_IN), .count(count), .Q(PC_q), .clk(CLK), .clr(in_1));  // open: carry
  Register u_A (.D(DATA_IN), .en(A), .Q(OUT_A), .clk(CLK), .clr(in_1));
  Register u_B (.D(DATA_IN), .en(B), .Q(OUT_B), .clk(CLK), .clr(in_1));
  Register u_C (.D(DATA_IN), .en(C), .Q(OUT_C), .clk(CLK), .clr(in_1));
  Register u_IN (.D(subtractor_1_out), .en(IN), .Q(IN_q), .clk(CLK), .clr(in_1));
  Register u_OUT (.D(DATA_IN), .en(OUT), .Q(OUT_q), .clk(CLK), .clr(in_1));
  Register u_IR (.D(DATA_IN), .en(IR), .Q({IR_q, IR_q_2}), .clk(CLK), .clr(in_1));
  RAM #(.bus("separate")) ram_1 (
    .addr(OUT_MAR), .din(DATA_IN), .data(ram_1_data), .str(str), .clk(CLK), .ld(ld));  // open: sel, clr
  Hex_Digit_Display hex_digit_display_1 (.value(OUT_MAR[7:4]));  // open: dp
  Hex_Digit_Display hex_digit_display_2 (.value(OUT_A[7:4]));  // open: dp
  Hex_Digit_Display hex_digit_display_3 (.value(OUT_q[7:4]));  // open: dp
  Hex_Digit_Display hex_digit_display_4 (.value(OUT_MAR[3:0]));  // open: dp
  Hex_Digit_Display hex_digit_display_5 (.value(OUT_A[3:0]));  // open: dp
  Hex_Digit_Display hex_digit_display_6 (.value(OUT_q[3:0]));  // open: dp
  ROM #(.dataWidth(20)) rom_1 (
    .addr({or_2_out[7], counter_1_q, IR_q}),
    .data({str, ld, bus, mar, count, ldcount, A, B, C, IN, OUT, IR, flags, OPC, clc, x}), .sel(1'b1));
  Hex_Digit_Display hex_digit_display_7 (.value(OUT_C[7:4]));  // open: dp
  Hex_Digit_Display hex_digit_display_8 (.value(OUT_ALU[7:4]));  // open: dp
  Hex_Digit_Display hex_digit_display_9 (.value(OUT_ALU[3:0]));  // open: dp
  Hex_Digit_Display hex_digit_display_10 (.value(OUT_B[7:4]));  // open: dp
  Hex_Digit_Display hex_digit_display_11 (.value(OUT_B[3:0]));  // open: dp
  Hex_Digit_Display hex_digit_display_12 (.value(OUT_C[3:0]));  // open: dp
  Multiplexer #(.select(3), .width(8)) multiplexer_1 (
    .in0(ram_1_data), .in1(PC_q), .in2(OUT_A), .in3(OUT_B), .in4(OUT_C), .in5(IN_q), .in6(OUT_ALU),
    .in7({4'b0000, IR_q_2}), .out(DATA_IN), .sel(bus));  // open: en

  // Other names for the same wires on the sheet: CLR = in_1

  // Notes on the sheet:
  //   contents of rom_1 (hex, n*v repeats v):
  //   16*c000 16*42040 2 3c000 38800 10400 10200 18800 20800 10080 3c000 24000 30200 30204 39000 2 100 0 0
  //   40800 6*2 90000 b8000 2 2 2 0 28800 0 0 2 6*0 2 2 4*0 2 49*0 16*c000 16*42040 2 3c000 38800 10400
  //   10200 18800 20800 10080 3c000 24000 30200 30204 39000 39000 100 0 0 40800 6*2 90000 b8000 4*2 28800
  //   0 0 2 6*0 2 2 4*0 2
endmodule

module \not  (
  input  in_1,
  output out_2
);

  Transistor transistor_1 (.in(1'b1), .out(out_2), .gate(in_1));
  Transistor #(.\type ("n")) transistor_2 (.in(1'b0), .out(out_2), .gate(in_1));
endmodule

module \nand  (
  input  in_1,
  input  in_2,
  output out_3
);

  wire transistor_4_out;

  Transistor transistor_1 (.in(1'b1), .out(out_3), .gate(in_1));
  Transistor transistor_2 (.in(1'b1), .out(out_3), .gate(in_2));
  Transistor #(.\type ("n")) transistor_3 (.in(transistor_4_out), .out(out_3), .gate(in_1));
  Transistor #(.\type ("n")) transistor_4 (.in(1'b0), .out(transistor_4_out), .gate(in_2));
endmodule

module reg_1bit_pdf (
  input  i,
  input  s,
  output out3
);

  wire transistor_1_out, transistor_4_out, transistor_5_out, transistor_8_out, transistor_9_out,
       transistor_13_out, transistor_16_out, transistor_17_out, transistor_20_out;

  Transistor transistor_1 (.in(1'b1), .out(transistor_1_out), .gate(i));
  Transistor transistor_2 (.in(1'b1), .out(transistor_1_out), .gate(i));
  Transistor #(.\type ("n")) transistor_3 (.in(transistor_4_out), .out(transistor_1_out), .gate(i));
  Transistor #(.\type ("n")) transistor_4 (.in(1'b0), .out(transistor_4_out), .gate(i));
  Transistor transistor_5 (.in(1'b1), .out(transistor_5_out), .gate(i));
  Transistor transistor_6 (.in(1'b1), .out(transistor_5_out), .gate(s));
  Transistor #(.\type ("n")) transistor_7 (.in(transistor_8_out), .out(transistor_5_out), .gate(i));
  Transistor #(.\type ("n")) transistor_8 (.in(1'b0), .out(transistor_8_out), .gate(s));
  Transistor transistor_9 (.in(1'b1), .out(transistor_9_out), .gate(s));
  Transistor transistor_10 (.in(1'b1), .out(out3), .gate(transistor_5_out));
  Transistor transistor_11 (.in(1'b1), .out(transistor_9_out), .gate(transistor_1_out));
  Transistor #(.\type ("n")) transistor_12 (.in(transistor_13_out), .out(transistor_9_out), .gate(s));
  Transistor #(.\type ("n")) transistor_13 (.in(1'b0), .out(transistor_13_out), .gate(transistor_1_out));
  Transistor transistor_14 (.in(1'b1), .out(out3), .gate(transistor_17_out));
  Transistor #(.\type ("n")) transistor_15 (.in(transistor_16_out), .out(out3), .gate(transistor_5_out));
  Transistor #(.\type ("n")) transistor_16 (.in(1'b0), .out(transistor_16_out), .gate(transistor_17_out));
  Transistor transistor_17 (.in(1'b1), .out(transistor_17_out), .gate(out3));
  Transistor transistor_18 (.in(1'b1), .out(transistor_17_out), .gate(transistor_9_out));
  Transistor #(.\type ("n")) transistor_19 (.in(transistor_20_out), .out(transistor_17_out), .gate(out3));
  Transistor #(.\type ("n")) transistor_20 (.in(1'b0), .out(transistor_20_out), .gate(transistor_9_out));
endmodule

module reg_1bit (
  input  in_1,
  input  in_2,
  output out_3
);

  wire nand_1_out_3, nand_2_out_3, nand_3_out_3, nand_5_out;

  \nand  nand_1 (.in_1(in_1), .in_2(in_1), .out_3(nand_1_out_3));
  \nand  nand_2 (.in_1(in_1), .in_2(in_2), .out_3(nand_2_out_3));
  \nand  nand_3 (.in_1(in_2), .in_2(nand_1_out_3), .out_3(nand_3_out_3));
  nand nand_4 (out_3, nand_2_out_3, nand_5_out);
  nand nand_5 (nand_5_out, out_3, nand_3_out_3);
endmodule

module reg_8biti (
  input  [7:0] in_1,
  input  s,
  output [7:0] out_3
);

  reg_1bit reg_1bit_1 (.in_1(in_1[0]), .in_2(s), .out_3(out_3[0]));
  reg_1bit reg_1bit_2 (.in_1(in_1[1]), .in_2(s), .out_3(out_3[1]));
  reg_1bit reg_1bit_3 (.in_1(in_1[2]), .in_2(s), .out_3(out_3[2]));
  reg_1bit reg_1bit_4 (.in_1(in_1[3]), .in_2(s), .out_3(out_3[3]));
  reg_1bit reg_1bit_5 (.in_1(in_1[4]), .in_2(s), .out_3(out_3[4]));
  reg_1bit reg_1bit_6 (.in_1(in_1[5]), .in_2(s), .out_3(out_3[5]));
  reg_1bit reg_1bit_7 (.in_1(in_1[6]), .in_2(s), .out_3(out_3[6]));
  reg_1bit reg_1bit_8 (.in_1(in_1[7]), .in_2(s), .out_3(out_3[7]));
endmodule

module \xor  (
  input  a,
  input  b,
  output out
);

  wire transistor_1_out, transistor_2_out, transistor_5_out, transistor_8_out, transistor_9_out,
       transistor_10_out, transistor_13_out, transistor_16_out, transistor_20_out;

  Transistor transistor_1 (.in(1'b1), .out(transistor_1_out), .gate(a));
  Transistor transistor_2 (.in(1'b1), .out(transistor_2_out), .gate(b));
  Transistor transistor_3 (.in(1'b1), .out(transistor_1_out), .gate(a));
  Transistor #(.\type ("n")) transistor_4 (.in(transistor_5_out), .out(transistor_1_out), .gate(a));
  Transistor #(.\type ("n")) transistor_5 (.in(1'b0), .out(transistor_5_out), .gate(a));
  Transistor transistor_6 (.in(1'b1), .out(transistor_2_out), .gate(b));
  Transistor #(.\type ("n")) transistor_7 (.in(transistor_8_out), .out(transistor_2_out), .gate(b));
  Transistor #(.\type ("n")) transistor_8 (.in(1'b0), .out(transistor_8_out), .gate(b));
  Transistor transistor_9 (.in(1'b1), .out(transistor_9_out), .gate(a));
  Transistor transistor_10 (.in(1'b1), .out(transistor_10_out), .gate(transistor_1_out));
  Transistor transistor_11 (.in(1'b1), .out(transistor_9_out), .gate(transistor_2_out));
  Transistor #(.\type ("n")) transistor_12 (.in(transistor_13_out), .out(transistor_9_out), .gate(a));
  Transistor #(.\type ("n")) transistor_13 (.in(1'b0), .out(transistor_13_out), .gate(transistor_2_out));
  Transistor transistor_14 (.in(1'b1), .out(transistor_10_out), .gate(b));
  Transistor #(.\type ("n")) transistor_15 (.in(transistor_16_out), .out(transistor_10_out), .gate(transistor_1_out));
  Transistor #(.\type ("n")) transistor_16 (.in(1'b0), .out(transistor_16_out), .gate(b));
  Transistor transistor_17 (.in(1'b1), .out(out), .gate(transistor_9_out));
  Transistor transistor_18 (.in(1'b1), .out(out), .gate(transistor_10_out));
  Transistor #(.\type ("n")) transistor_19 (.in(transistor_20_out), .out(out), .gate(transistor_9_out));
  Transistor #(.\type ("n")) transistor_20 (.in(1'b0), .out(transistor_20_out), .gate(transistor_10_out));
endmodule

module sum_1bit (
  input  a,
  input  b,
  input  cin,
  output s,
  output cout
);

  wire nand_1_out_3, nand_2_out_3, not_1_out_2, not_2_out_2, xor_1_out;

  \xor  xor_1 (.a(a), .b(b), .out(xor_1_out));
  \nand  nand_1 (.in_1(cin), .in_2(xor_1_out), .out_3(nand_1_out_3));
  \nand  nand_2 (.in_1(a), .in_2(b), .out_3(nand_2_out_3));
  \xor  xor_2 (.a(xor_1_out), .b(cin), .out(s));
  \not  not_1 (.in_1(nand_1_out_3), .out_2(not_1_out_2));
  \not  not_2 (.in_1(nand_2_out_3), .out_2(not_2_out_2));
  \xor  xor_3 (.a(not_1_out_2), .b(not_2_out_2), .out(cout));
endmodule

module mux2_1 (
  input  in_1,
  input  in_2,
  input  in_3,
  output out
);

  wire transistor_1_out, transistor_4_out, transistor_5_out, transistor_6_out, transistor_9_out,
       transistor_12_out, transistor_16_out;

  Transistor transistor_1 (.in(1'b1), .out(transistor_1_out), .gate(in_2));
  Transistor transistor_2 (.in(1'b1), .out(transistor_1_out), .gate(in_2));
  Transistor #(.\type ("n")) transistor_3 (.in(transistor_4_out), .out(transistor_1_out), .gate(in_2));
  Transistor #(.\type ("n")) transistor_4 (.in(1'b0), .out(transistor_4_out), .gate(in_2));
  Transistor transistor_5 (.in(1'b1), .out(transistor_5_out), .gate(transistor_1_out));
  Transistor transistor_6 (.in(1'b1), .out(transistor_6_out), .gate(in_1));
  Transistor transistor_7 (.in(1'b1), .out(transistor_5_out), .gate(in_3));
  Transistor #(.\type ("n")) transistor_8 (.in(transistor_9_out), .out(transistor_5_out), .gate(transistor_1_out));
  Transistor #(.\type ("n")) transistor_9 (.in(1'b0), .out(transistor_9_out), .gate(in_3));
  Transistor transistor_10 (.in(1'b1), .out(transistor_6_out), .gate(in_2));
  Transistor #(.\type ("n")) transistor_11 (.in(transistor_12_out), .out(transistor_6_out), .gate(in_1));
  Transistor #(.\type ("n")) transistor_12 (.in(1'b0), .out(transistor_12_out), .gate(in_2));
  Transistor transistor_13 (.in(1'b1), .out(out), .gate(transistor_5_out));
  Transistor transistor_14 (.in(1'b1), .out(out), .gate(transistor_6_out));
  Transistor #(.\type ("n")) transistor_15 (.in(transistor_16_out), .out(out), .gate(transistor_6_out));
  Transistor #(.\type ("n")) transistor_16 (.in(1'b0), .out(transistor_16_out), .gate(transistor_5_out));

  // Other names for the same wires on the sheet: a = in_3; b = in_1; s = in_2
endmodule

module sum_8bit (
  input  Cin,
  input  [7:0] A,
  input  [7:0] B,
  output [7:0] Out,
  output Cout
);

  wire sum_1bit_1_cout, sum_1bit_2_cout, sum_1bit_3_cout, sum_1bit_4_cout, sum_1bit_5_cout, sum_1bit_6_cout,
       sum_1bit_7_cout;

  sum_1bit sum_1bit_1 (.a(A[0]), .b(B[0]), .cin(Cin), .s(Out[0]), .cout(sum_1bit_1_cout));
  sum_1bit sum_1bit_2 (.a(A[1]), .b(B[1]), .cin(sum_1bit_1_cout), .s(Out[1]), .cout(sum_1bit_2_cout));
  sum_1bit sum_1bit_3 (.a(A[2]), .b(B[2]), .cin(sum_1bit_2_cout), .s(Out[2]), .cout(sum_1bit_3_cout));
  sum_1bit sum_1bit_4 (.a(A[3]), .b(B[3]), .cin(sum_1bit_3_cout), .s(Out[3]), .cout(sum_1bit_4_cout));
  sum_1bit sum_1bit_5 (.a(A[4]), .b(B[4]), .cin(sum_1bit_4_cout), .s(Out[4]), .cout(sum_1bit_5_cout));
  sum_1bit sum_1bit_6 (.a(A[5]), .b(B[5]), .cin(sum_1bit_5_cout), .s(Out[5]), .cout(sum_1bit_6_cout));
  sum_1bit sum_1bit_7 (.a(A[6]), .b(B[6]), .cin(sum_1bit_6_cout), .s(Out[6]), .cout(sum_1bit_7_cout));
  sum_1bit sum_1bit_8 (.a(A[7]), .b(B[7]), .cin(sum_1bit_7_cout), .s(Out[7]), .cout(Cout));
endmodule

module noter (
  input  [7:0] b,
  input  Cin,
  output [7:0] out_3
);

  \xor  xor_1 (.a(b[7]), .b(Cin), .out(out_3[7]));
  \xor  xor_2 (.a(b[6]), .b(Cin), .out(out_3[6]));
  \xor  xor_3 (.a(b[5]), .b(Cin), .out(out_3[5]));
  \xor  xor_4 (.a(b[4]), .b(Cin), .out(out_3[4]));
  \xor  xor_5 (.a(b[3]), .b(Cin), .out(out_3[3]));
  \xor  xor_6 (.a(b[2]), .b(Cin), .out(out_3[2]));
  \xor  xor_7 (.a(b[1]), .b(Cin), .out(out_3[1]));
  \xor  xor_8 (.a(b[0]), .b(Cin), .out(out_3[0]));
endmodule

module ALU (
  input  [7:0] a,
  input  [7:0] b,
  input  Cin,
  output [7:0] out,
  output Cout
);

  wire [7:0] noter_1_out_3;

  noter noter_1 (.b(b), .Cin(Cin), .out_3(noter_1_out_3));
  sum_8bit sum_8bit_1 (.Cin(Cin), .A(a), .B(noter_1_out_3), .Out(out), .Cout(Cout));
endmodule

module dec2_4 (
  input  in_1,
  input  in_2,
  output out_3,
  output out_4,
  output out_5,
  output out_6
);

  wire transistor_1_out, transistor_2_out, transistor_5_out, transistor_8_out, transistor_9_out,
       transistor_10_out, transistor_11_out, transistor_12_out, transistor_15_out, transistor_18_out,
       transistor_21_out, transistor_24_out, transistor_31_out, transistor_34_out, transistor_37_out,
       transistor_40_out;

  Transistor transistor_1 (.in(1'b1), .out(transistor_1_out), .gate(in_1));
  Transistor transistor_2 (.in(1'b1), .out(transistor_2_out), .gate(in_2));
  Transistor transistor_3 (.in(1'b1), .out(transistor_1_out), .gate(in_1));
  Transistor #(.\type ("n")) transistor_4 (.in(transistor_5_out), .out(transistor_1_out), .gate(in_1));
  Transistor #(.\type ("n")) transistor_5 (.in(1'b0), .out(transistor_5_out), .gate(in_1));
  Transistor transistor_6 (.in(1'b1), .out(transistor_2_out), .gate(in_2));
  Transistor #(.\type ("n")) transistor_7 (.in(transistor_8_out), .out(transistor_2_out), .gate(in_2));
  Transistor #(.\type ("n")) transistor_8 (.in(1'b0), .out(transistor_8_out), .gate(in_2));
  Transistor transistor_9 (.in(1'b1), .out(transistor_9_out), .gate(transistor_2_out));
  Transistor transistor_10 (.in(1'b1), .out(transistor_10_out), .gate(in_2));
  Transistor transistor_11 (.in(1'b1), .out(transistor_11_out), .gate(in_1));
  Transistor transistor_12 (.in(1'b1), .out(transistor_12_out), .gate(in_2));
  Transistor transistor_13 (.in(1'b1), .out(transistor_9_out), .gate(transistor_1_out));
  Transistor #(.\type ("n")) transistor_14 (.in(transistor_15_out), .out(transistor_9_out), .gate(transistor_1_out));
  Transistor #(.\type ("n")) transistor_15 (.in(1'b0), .out(transistor_15_out), .gate(transistor_2_out));
  Transistor transistor_16 (.in(1'b1), .out(transistor_10_out), .gate(transistor_1_out));
  Transistor #(.\type ("n")) transistor_17 (.in(transistor_18_out), .out(transistor_10_out), .gate(transistor_1_out));
  Transistor #(.\type ("n")) transistor_18 (.in(1'b0), .out(transistor_18_out), .gate(in_2));
  Transistor transistor_19 (.in(1'b1), .out(transistor_11_out), .gate(transistor_2_out));
  Transistor #(.\type ("n")) transistor_20 (.in(transistor_21_out), .out(transistor_11_out), .gate(transistor_2_out));
  Transistor #(.\type ("n")) transistor_21 (.in(1'b0), .out(transistor_21_out), .gate(in_1));
  Transistor transistor_22 (.in(1'b1), .out(transistor_12_out), .gate(in_1));
  Transistor #(.\type ("n")) transistor_23 (.in(transistor_24_out), .out(transistor_12_out), .gate(in_1));
  Transistor #(.\type ("n")) transistor_24 (.in(1'b0), .out(transistor_24_out), .gate(in_2));
  Transistor transistor_25 (.in(1'b1), .out(out_3), .gate(transistor_9_out));
  Transistor transistor_26 (.in(1'b1), .out(out_4), .gate(transistor_10_out));
  Transistor transistor_27 (.in(1'b1), .out(out_5), .gate(transistor_11_out));
  Transistor transistor_28 (.in(1'b1), .out(out_6), .gate(transistor_12_out));
  Transistor transistor_29 (.in(1'b1), .out(out_3), .gate(transistor_9_out));
  Transistor #(.\type ("n")) transistor_30 (.in(transistor_31_out), .out(out_3), .gate(transistor_9_out));
  Transistor #(.\type ("n")) transistor_31 (.in(1'b0), .out(transistor_31_out), .gate(transistor_9_out));
  Transistor transistor_32 (.in(1'b1), .out(out_4), .gate(transistor_10_out));
  Transistor #(.\type ("n")) transistor_33 (.in(transistor_34_out), .out(out_4), .gate(transistor_10_out));
  Transistor #(.\type ("n")) transistor_34 (.in(1'b0), .out(transistor_34_out), .gate(transistor_10_out));
  Transistor transistor_35 (.in(1'b1), .out(out_5), .gate(transistor_11_out));
  Transistor #(.\type ("n")) transistor_36 (.in(transistor_37_out), .out(out_5), .gate(transistor_11_out));
  Transistor #(.\type ("n")) transistor_37 (.in(1'b0), .out(transistor_37_out), .gate(transistor_11_out));
  Transistor transistor_38 (.in(1'b1), .out(out_6), .gate(transistor_12_out));
  Transistor #(.\type ("n")) transistor_39 (.in(transistor_40_out), .out(out_6), .gate(transistor_12_out));
  Transistor #(.\type ("n")) transistor_40 (.in(1'b0), .out(transistor_40_out), .gate(transistor_12_out));
endmodule

module reg1bit_CLK_EN (
  input  i,
  input  EN,
  output out_3
);

  wire clock_1_out, nand_1_out_3, nand_2_out_3, nand_3_out_3, nand_4_out_3, nand_5_out_3, nand_7_out;

  Clock clock_1 (.out(clock_1_out));
  \nand  nand_1 (.in_1(EN), .in_2(clock_1_out), .out_3(nand_1_out_3));
  \nand  nand_2 (.in_1(nand_1_out_3), .in_2(nand_1_out_3), .out_3(nand_2_out_3));
  \nand  nand_3 (.in_1(i), .in_2(i), .out_3(nand_3_out_3));
  \nand  nand_4 (.in_1(i), .in_2(nand_2_out_3), .out_3(nand_4_out_3));
  \nand  nand_5 (.in_1(nand_2_out_3), .in_2(nand_3_out_3), .out_3(nand_5_out_3));
  nand nand_6 (out_3, nand_4_out_3, nand_7_out);
  nand nand_7 (nand_7_out, out_3, nand_5_out_3);
endmodule
